// Logisim project real alu.circ as structural Verilog
module a_AND_b (
  input  [7:0] in_1,
  input  [7:0] in_2,
  output [7:0] out_3
);

  assign out_3 = in_1 & in_2;  // AND_Gate and_1, 8 bits wide
endmodule

module a_OR_b (
  input  [7:0] in_1,
  input  [7:0] in_2,
  output [7:0] out_3
);

  assign out_3 = in_1 | in_2;  // OR_Gate or_1, 8 bits wide
endmodule

module NOT_b (
  input  [7:0] in_1,
  output [7:0] out_2
);

  assign out_2 = in_1;  // Buffer buffer_1, 8 bits wide
endmodule

module half_adder (
  input  a,
  input  b,
  output out_3,
  output out_4
);

  xor xor_1 (out_3, a, b);
  and and_1 (out_4, a, b);
endmodule

module full_adder (
  input  in_1,
  input  in_2,
  input  in_3,
  output out_4,
  output out_5
);

  wire and_1_out, and_2_out, and_3_out, xor_1_out;

  xor xor_1 (xor_1_out, in_3, in_2);
  and and_1 (and_1_out, in_1, in_2);
  and and_2 (and_2_out, in_3, in_2);
  and and_3 (and_3_out, in_3, in_1);
  xor xor_2 (out_4, xor_1_out, in_1);
  or or_1 (out_5, and_1_out, and_2_out, and_3_out);
endmodule

module LSL_b (
  input  [7:0] in_1,
  output [7:0] out_2,
  output out_3
);

  main main_1 ();

  assign out_2 = {in_1[6:0], 1'b0};
  assign out_3 = in_1[7];
endmodule

module LSR_b (
  input  [7:0] in_1,
  output out_2,
  output [7:0] out_3
);


  assign out_2 = in_1[0];
  assign out_3 = {1'b0, in_1[7:1]};
endmodule
